# Fritzing sketch Scheme (saved by Fritzing 0.9.3b)

parts:
  U1 = ESP8266 NodeMCU LoLin module
  U2 = 4-Channel 5v Relay Shield [package=relay-4ch5v10a]

nets:
  N1: U1.D0, U2.IN1
  N2: U1.D1, U2.IN2
  N3: U1.D2, U2.IN3
  N4: U1.D3, U2.IN4
  VIN: U1.Vin, U2.VCC
  GND: U1.GND, U2.GND
  N5: U2.K1-Off, U2.K2-Off, U2.K3-Off, U2.K4-Off

custom parts:
  ESP8266 NodeMCU LoLin module: ESP8266 based NodeMCU
  4-Channel 5v Relay Shield: 4 Channel 5v Relay Shield w. 2x SPD-06VDC-SD-C
